# Fritzing sketch испыт.1 (saved by Fritzing 0.9.3b)
breadboards: 1

parts:
  Arduino1 = Arduino Mini (Rev5)
  R1 = Resistor [tolerance=±5% resistance=5.1k package=THT]
  R2 = Resistor [tolerance=±5% resistance=5.1k package=THT]
  RHT1 = Humidity and Temperature Sensor RHT03

nets:
  N1: Arduino1.D4, RHT1.Data-signal
  5V: Arduino1.5V, R1.Pin_1, R2.Pin_1, RHT1.Vcc
  N2: Arduino1.A4, R1.Pin_0
  N3: Arduino1.A5, R2.Pin_0
